# Fritzing sketch AwesomeStudioPedal_esp32_wiring (saved by Fritzing 1.0.6)
circuit board: 11.9314cm x 5.75743cm
breadboards: 1

parts:
  Button_D = Pushbutton [package="[THT]"]
  Button_Select = Pushbutton [package="[THT]"]
  Button_C = Pushbutton [package="[THT]"]
  Button_A = Pushbutton [package="[THT]"]
  U1 = ESP32S-HiLetgo [part_number=ESP32S-HiLetgo]
  Button_B = Pushbutton [package="[THT]"]
  R_PWR = Resistor [tolerance=±5% power=0.25W resistance=680 package=THT]
  R_LED_1 = Resistor [tolerance=±5% power=0.25W resistance=680 package=THT]
  R_LED_2 = Resistor [tolerance=±5% power=0.25W resistance=680 package=THT]
  R_LED_3 = Resistor [tolerance=±5% power=0.25W resistance=680 package=THT]
  R_LED_BLE = Resistor [tolerance=±5% power=0.25W resistance=680 package=THT]
  R_LED_C = Resistor [tolerance=±5% power=0.25W resistance=680 package=THT]
  R_LED_A = Resistor [tolerance=±5% power=0.25W resistance=680 package=THT]
  R_LED_B = Resistor [tolerance=±5% power=0.25W resistance=680 package=THT]
  R_LED_D = Resistor [tolerance=±5% power=0.25W resistance=680 package=THT]
  R_Select = Resistor [tolerance=±5% power=0.25W resistance=3.3k package=THT]
  R_D = Resistor [tolerance=±5% power=0.25W resistance=3.3k package=THT]
  R_B = Resistor [tolerance=±5% power=0.25W resistance=3.3k package=THT]
  R_C = Resistor [tolerance=±5% power=0.25W resistance=3.3k package=THT]
  LED_PWR = LED - 5mm [color="Green (565nm)" current=0.030A package="5 mm [THT]"]
  LED_3 = LED - 5mm [color="Yellow (592nm)" current=0.030A package="5 mm [THT]"]
  LED_2 = LED - 5mm [color="Yellow (592nm)" current=0.030A package="5 mm [THT]"]
  LED_1 = LED - 5mm [color="Yellow (592nm)" current=0.030A package="5 mm [THT]"]
  LED_BLE = LED - 5mm [color="Blue (525nm)" current=0.030A package="5 mm [THT]"]
  LED_A = LED - 5mm [color="Red (660nm)" current=0.030A package="5 mm [THT]"]
  LED_B = LED - 5mm [color="Red (660nm)" current=0.030A package="5 mm [THT]"]
  LED_C = LED - 5mm [color="Red (660nm)" current=0.030A package="5 mm [THT]"]
  LED_D = LED - 5mm [color="Red (660nm)" current=0.030A package="5 mm [THT]"]
  R_A = Resistor [tolerance=±5% power=0.25W resistance=3.3k package=THT]

nets:
  N1: Button_D.Pin_1, Button_D.Pin_2, U1.GPIO13, R_D.Pin_1, LED_D.cathode
  N2: Button_D.Pin_3, Button_D.Pin_4, Button_Select.Pin_1, Button_Select.Pin_2, Button_C.Pin_3, Button_C.Pin_4, Button_A.Pin_3, Button_A.Pin_4, U1.GND, Button_B.Pin_3, Button_B.Pin_4, LED_PWR.cathode
  N3: Button_Select.Pin_3, Button_Select.Pin_4, U1.3.3, U1.GPIO21, R_PWR.Pin_0, R_PWR.Pin_1, R_LED_1.Pin_0, R_LED_2.Pin_0, R_LED_3.Pin_0, R_LED_BLE.Pin_0, R_LED_C.Pin_0, R_LED_A.Pin_0, R_LED_B.Pin_0, R_LED_D.Pin_0, R_Select.Pin_0, R_Select.Pin_1, R_D.Pin_0, R_B.Pin_0, R_C.Pin_0, LED_PWR.anode, R_A.Pin_0
  N4: Button_C.Pin_1, Button_C.Pin_2, U1.GPIO12, R_C.Pin_1, LED_C.cathode
  N5: Button_A.Pin_1, Button_A.Pin_2, U1.GPIO27, LED_A.cathode, R_A.Pin_1
  N6: U1.GPIO26, LED_BLE.cathode
  N7: U1.GPIO14, Button_B.Pin_1, Button_B.Pin_2, R_B.Pin_1, LED_B.cathode
  N8: U1.GPIO5, LED_3.cathode
  N9: U1.GPIO18, LED_2.cathode
  N10: U1.GPIO19, LED_1.cathode
  N11: R_LED_1.Pin_1, LED_1.anode
  N12: R_LED_2.Pin_1, LED_2.anode
  N13: R_LED_3.Pin_1, LED_3.anode
  N14: R_LED_BLE.Pin_1, LED_BLE.anode
  N15: R_LED_C.Pin_1, LED_C.anode
  N16: R_LED_A.Pin_1, LED_A.anode
  N17: R_LED_B.Pin_1, LED_B.anode
  N18: R_LED_D.Pin_1, LED_D.anode

custom parts:
  ESP32S-HiLetgo: HiLetgo ESP-WROOM-32 ESP32 ESP-32S Development Board 2.4GHz Dual-Mode WiFi + Bluetooth Dual Cores Microcontroller The ESP32 integrated with Antenna switches, RF Balun, power amplifiers, low-noise amplifiers, filters, and management modules, and the entire solution occupies the least area of PCB. 2.4 GHz Wi-Fi plus Bluetooth dual-mode chip, with TSMC Ultra-low power consumption 40nm technology,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
